// Logisim project Lab1.circ as structural Verilog: 1 circuit, main circuit main
module main (
  input  [7:0] A,
  input  [2:0] B,
  output [7:0] Y
);

  Multiplexer #(.select(3), .width(8), .enable("false")) multiplexer_1 (
    .in0(A), .in1({A[6:0], 1'b0}), .in2({A[5:0], 2'b00}), .in3({A[4:0], 3'b000}), .in4({A[3:0], 4'b0000}),
    .in5({A[2:0], {5{1'b0}}}), .in6({A[1:0], {6{1'b0}}}), .in7({A[0], {7{1'b0}}}), .out(Y), .sel(B));
endmodule
