// Logisim project alu.circ as structural Verilog: 10 circuits, main circuit main
module main (
  input  [15:0] A,
  input  [15:0] B,
  input  [3:0] Control,
  output [15:0] out_4
);

  wire [15:0] arithmetic_unit_1_f, logic_unit_1_out, shift_unit_1_out_4;

  arithmetic_unit arithmetic_unit_1 (.A(A), .B(B), .Control(Control[1:0]), .F(arithmetic_unit_1_f));
  logic_unit logic_unit_1 (.A(A), .B(B), .Control(Control[1:0]), .Out(logic_unit_1_out));
  shift_unit shift_unit_1 (.A(A), .B(B), .Control(Control[1:0]), .out_4(shift_unit_1_out_4));
  Multiplexer #(.select(2), .width(16), .enable("false")) multiplexer_1 (
    .in0({16{1'b0}}), .in1(arithmetic_unit_1_f), .in2(logic_unit_1_out), .in3(shift_unit_1_out_4),
    .out(out_4), .sel(Control[3:2]));
endmodule

// FA
module full_adder (
  input  Cin,
  input  A,
  input  B,
  output Sum,
  output Cout
);

  wire and_1_out, and_2_out, xor_1_out;

  xor xor_1 (xor_1_out, A, B);
  xor xor_2 (Sum, xor_1_out, Cin);
  and and_1 (and_1_out, Cin, xor_1_out);
  or or_1 (Cout, and_1_out, and_2_out);
  and and_2 (and_2_out, A, B);
  // AND_Gate and_3 is placed but not wired

  // Notes on the sheet:
  //   Full Adder
endmodule

// LU
module logic_unit (
  input  [15:0] A,
  input  [15:0] B,
  input  [1:0] Control,
  output [15:0] Out
);

  logic_block logic_block_1 (.A(A[0]), .B(B[0]), .Control(Control), .F(Out[0]));
  logic_block logic_block_2 (.A(A[1]), .B(B[1]), .Control(Control), .F(Out[1]));
  logic_block logic_block_3 (.A(A[2]), .B(B[2]), .Control(Control), .F(Out[2]));
  logic_block logic_block_4 (.A(A[3]), .B(B[3]), .Control(Control), .F(Out[3]));
  logic_block logic_block_5 (.A(A[4]), .B(B[4]), .Control(Control), .F(Out[4]));
  logic_block logic_block_6 (.A(A[5]), .B(B[5]), .Control(Control), .F(Out[5]));
  logic_block logic_block_7 (.A(A[6]), .B(B[6]), .Control(Control), .F(Out[6]));
  logic_block logic_block_8 (.A(A[7]), .B(B[7]), .Control(Control), .F(Out[7]));
  logic_block logic_block_9 (.A(A[8]), .B(B[8]), .Control(Control), .F(Out[8]));
  logic_block logic_block_10 (.A(A[9]), .B(B[9]), .Control(Control), .F(Out[9]));
  logic_block logic_block_11 (.A(A[10]), .B(B[10]), .Control(Control), .F(Out[10]));
  logic_block logic_block_12 (.A(A[11]), .B(B[11]), .Control(Control), .F(Out[11]));
  logic_block logic_block_13 (.A(A[12]), .B(B[12]), .Control(Control), .F(Out[12]));
  logic_block logic_block_14 (.A(A[13]), .B(B[13]), .Control(Control), .F(Out[13]));
  logic_block logic_block_15 (.A(A[14]), .B(B[14]), .Control(Control), .F(Out[14]));
  logic_block logic_block_16 (.A(A[15]), .B(B[15]), .Control(Control), .F(Out[15]));
endmodule

// SU
module shift_unit (
  input  [1:0] Control,
  input  [15:0] A,
  input  [15:0] B,
  output [15:0] out_4
);

  wire [15:0] lls_1_out_3, right_shift_1_out_4, right_shift_2_out_4;

  right_shift right_shift_1 (.Mode(1'b0), .out_4(right_shift_1_out_4), .A(A), .B(B[3:0]));
  right_shift right_shift_2 (.Mode(1'b1), .out_4(right_shift_2_out_4), .A(A), .B(B[3:0]));
  LLS lls_1 (.out_3(lls_1_out_3), .A(A), .B(B[3:0]));
  Multiplexer #(.select(2), .width(16), .enable("false")) multiplexer_1 (
    .in0(lls_1_out_3), .in1(right_shift_1_out_4), .in2(right_shift_2_out_4), .in3({16{1'b0}}), .out(out_4),
    .sel(Control));
endmodule

module LLS (
  input  [3:0] B,
  input  [15:0] A,
  output [15:0] out_3
);

  Multiplexer #(.select(4), .width(16), .enable("false")) multiplexer_1 (
    .in0({{2{A[15]}}, A[13:0]}), .in1({A[15], A[13:0], 1'b0}), .in2({A[13:0], 2'b00}),
    .in3({A[12:0], 3'b000}), .in4({A[11:0], 4'b0000}), .in5({A[10:0], {5{1'b0}}}), .in6({A[9:0], {6{1'b0}}}),
    .in7({A[8:0], {7{1'b0}}}), .in8({A[7:0], {8{1'b0}}}), .in9({A[6:0], {9{1'b0}}}),
    .in10({A[5:0], {10{1'b0}}}), .in11({A[4:0], {11{1'b0}}}), .in12({A[3:0], {12{1'b0}}}),
    .in13({A[2:0], {13{1'b0}}}), .in14({A[1:0], {14{1'b0}}}), .in15({A[0], {15{1'b0}}}), .out(out_3), .sel(B));

  assign A[14] = A[15];
endmodule

module right_shift (
  input  [3:0] B,
  input  [15:0] A,
  input  Mode,
  output [15:0] out_4
);

  wire [15:15] and_1_out;

  and and_1 (and_1_out[15], Mode, A[15]);
  Multiplexer #(.select(4), .width(16), .enable("false")) multiplexer_1 (
    .in0(A), .in1({and_1_out[15], A[15:1]}), .in2({{2{and_1_out[15]}}, A[15:2]}),
    .in3({{3{and_1_out[15]}}, A[15:3]}), .in4({{4{and_1_out[15]}}, A[15:4]}),
    .in5({{5{and_1_out[15]}}, A[15:5]}), .in6({{6{and_1_out[15]}}, A[15:6]}),
    .in7({{7{and_1_out[15]}}, A[15:7]}), .in8({{8{and_1_out[15]}}, A[15:8]}),
    .in9({{9{and_1_out[15]}}, A[15:9]}), .in10({{10{and_1_out[15]}}, A[15:10]}),
    .in11({{11{and_1_out[15]}}, A[15:11]}), .in12({{12{and_1_out[15]}}, A[15:12]}),
    .in13({{13{and_1_out[15]}}, A[15:13]}), .in14({{14{and_1_out[15]}}, A[15:14]}),
    .in15({{15{and_1_out[15]}}, A[15]}), .out(out_4), .sel(B));
endmodule

// AU
module arithmetic_unit (
  input  [15:0] A,
  input  [15:0] B,
  input  [1:0] Control,
  output [15:0] F
);

  wire [7:0] n4x4multiplier_1_product;
  wire [15:0] n16bit_adder_1_s, n16bit_adder_2_s, not_1_out;

  _16bit_adder u_16bit_adder_1 (.A(A), .B(B), .Cin(1'b0), .S(n16bit_adder_1_s));
  assign not_1_out = ~B;  // NOT_Gate not_1, 16 bits wide
  _16bit_adder u_16bit_adder_2 (.A(A), .B(not_1_out), .Cin(1'b1), .S(n16bit_adder_2_s));
  _4x4multiplier u_4x4multiplier_1 (.A(A[3:0]), .B(B[3:0]), .product(n4x4multiplier_1_product));
  Multiplexer #(.select(2), .width(16), .enable("false")) multiplexer_1 (
    .in0(n16bit_adder_1_s), .in1(n16bit_adder_2_s), .in2({{8{1'b0}}, n4x4multiplier_1_product}),
    .in3({16{1'b0}}), .out(F), .sel(Control));
endmodule

module _16bit_adder (
  input  [15:0] A,
  input  [15:0] B,
  input  Cin,
  output [15:0] S
);

  wire full_adder_1_cout, full_adder_2_cout, full_adder_3_cout, full_adder_4_cout, full_adder_5_cout,
       full_adder_6_cout, full_adder_7_cout, full_adder_8_cout, full_adder_9_cout, full_adder_10_cout,
       full_adder_11_cout, full_adder_12_cout, full_adder_13_cout, full_adder_14_cout, full_adder_15_cout;

  full_adder full_adder_1 (.A(A[0]), .B(B[0]), .Sum(S[0]), .Cin(Cin), .Cout(full_adder_1_cout));
  full_adder full_adder_2 (.A(A[1]), .B(B[1]), .Sum(S[1]), .Cin(full_adder_1_cout), .Cout(full_adder_2_cout));
  full_adder full_adder_3 (.A(A[2]), .B(B[2]), .Sum(S[2]), .Cin(full_adder_2_cout), .Cout(full_adder_3_cout));
  full_adder full_adder_4 (.A(A[3]), .B(B[3]), .Sum(S[3]), .Cin(full_adder_3_cout), .Cout(full_adder_4_cout));
  full_adder full_adder_5 (.A(A[4]), .B(B[4]), .Sum(S[4]), .Cin(full_adder_4_cout), .Cout(full_adder_5_cout));
  full_adder full_adder_6 (.A(A[5]), .B(B[5]), .Sum(S[5]), .Cin(full_adder_5_cout), .Cout(full_adder_6_cout));
  full_adder full_adder_7 (.A(A[6]), .B(B[6]), .Sum(S[6]), .Cin(full_adder_6_cout), .Cout(full_adder_7_cout));
  full_adder full_adder_8 (.A(A[7]), .B(B[7]), .Sum(S[7]), .Cin(full_adder_7_cout), .Cout(full_adder_8_cout));
  full_adder full_adder_9 (.A(A[8]), .B(B[8]), .Sum(S[8]), .Cin(full_adder_8_cout), .Cout(full_adder_9_cout));
  full_adder full_adder_10 (.A(A[9]), .B(B[9]), .Sum(S[9]), .Cin(full_adder_9_cout), .Cout(full_adder_10_cout));
  full_adder full_adder_11 (.A(A[10]), .B(B[10]), .Sum(S[10]), .Cin(full_adder_10_cout), .Cout(full_adder_11_cout));
  full_adder full_adder_12 (.A(A[11]), .B(B[11]), .Sum(S[11]), .Cin(full_adder_11_cout), .Cout(full_adder_12_cout));
  full_adder full_adder_13 (.A(A[12]), .B(B[12]), .Sum(S[12]), .Cin(full_adder_12_cout), .Cout(full_adder_13_cout));
  full_adder full_adder_14 (.A(A[13]), .B(B[13]), .Sum(S[13]), .Cin(full_adder_13_cout), .Cout(full_adder_14_cout));
  full_adder full_adder_15 (.A(A[14]), .B(B[14]), .Sum(S[14]), .Cin(full_adder_14_cout), .Cout(full_adder_15_cout));
  full_adder full_adder_16 (.A(A[15]), .B(B[15]), .Sum(S[15]), .Cin(full_adder_15_cout));  // open: Cout
endmodule

module _4x4multiplier (
  input  [3:0] A,
  input  [3:0] B,
  output [7:0] product
);

  wire and_1_out, and_2_out, and_3_out, and_4_out, and_5_out, and_6_out, and_7_out, and_8_out, and_9_out,
       and_10_out, and_11_out, and_12_out, and_13_out, and_14_out, and_16_out, full_adder_2_cout,
       full_adder_2_sum, full_adder_3_cout, full_adder_3_sum, full_adder_4_cout, full_adder_4_sum,
       full_adder_5_cout, full_adder_6_cout, full_adder_7_cout, full_adder_7_sum, full_adder_8_cout,
       full_adder_8_sum, full_adder_9_cout, full_adder_10_cout, full_adder_10_sum, full_adder_11_cout,
       full_adder_12_cout;

  and and_1 (and_1_out, A[3], B[2]);
  and and_2 (and_2_out, A[3], B[3]);
  and and_3 (and_3_out, A[2], B[3]);
  full_adder full_adder_1 (
    .A(full_adder_4_cout), .B(and_2_out), .Sum(product[6]), .Cin(full_adder_6_cout), .Cout(product[7]));
  and and_4 (and_4_out, A[3], B[1]);
  full_adder full_adder_2 (
    .A(1'b0), .B(and_4_out), .Sum(full_adder_2_sum), .Cin(full_adder_7_cout), .Cout(full_adder_2_cout));
  and and_5 (and_5_out, A[2], B[2]);
  full_adder full_adder_3 (
    .A(full_adder_2_sum), .B(and_5_out), .Sum(full_adder_3_sum), .Cin(full_adder_8_cout),
    .Cout(full_adder_3_cout));
  full_adder full_adder_4 (
    .A(full_adder_2_cout), .B(and_1_out), .Sum(full_adder_4_sum), .Cin(full_adder_3_cout),
    .Cout(full_adder_4_cout));
  and and_6 (and_6_out, A[1], B[3]);
  full_adder full_adder_5 (
    .A(full_adder_3_sum), .B(and_6_out), .Sum(product[4]), .Cin(full_adder_9_cout), .Cout(full_adder_5_cout));
  full_adder full_adder_6 (
    .A(full_adder_4_sum), .B(and_3_out), .Sum(product[5]), .Cin(full_adder_5_cout), .Cout(full_adder_6_cout));
  and and_7 (and_7_out, A[3], B[0]);
  and and_8 (and_8_out, A[2], B[1]);
  full_adder full_adder_7 (
    .A(and_7_out), .B(and_8_out), .Sum(full_adder_7_sum), .Cin(full_adder_10_cout), .Cout(full_adder_7_cout));
  and and_9 (and_9_out, A[1], B[2]);
  full_adder full_adder_8 (
    .A(full_adder_7_sum), .B(and_9_out), .Sum(full_adder_8_sum), .Cin(full_adder_11_cout),
    .Cout(full_adder_8_cout));
  and and_10 (and_10_out, A[0], B[3]);
  full_adder full_adder_9 (
    .A(full_adder_8_sum), .B(and_10_out), .Sum(product[3]), .Cin(1'b0), .Cout(full_adder_9_cout));
  and and_11 (and_11_out, A[2], B[0]);
  and and_12 (and_12_out, A[0], B[1]);
  and and_13 (and_13_out, A[1], B[1]);
  full_adder full_adder_10 (
    .A(and_11_out), .B(and_13_out), .Sum(full_adder_10_sum), .Cin(full_adder_12_cout),
    .Cout(full_adder_10_cout));
  and and_14 (and_14_out, A[0], B[2]);
  full_adder full_adder_11 (
    .A(full_adder_10_sum), .B(and_14_out), .Sum(product[2]), .Cin(1'b0), .Cout(full_adder_11_cout));
  and and_15 (product[0], A[0], B[0]);
  and and_16 (and_16_out, A[1], B[0]);
  full_adder full_adder_12 (.A(and_16_out), .B(and_12_out), .Sum(product[1]), .Cin(1'b0), .Cout(full_adder_12_cout));
endmodule

// LU
module logic_block (
  input  [1:0] Control,
  input  A,
  input  B,
  output F
);

  wire and_1_out, not_1_out, or_1_out, xor_1_out;

  or or_1 (or_1_out, A, B);
  not not_1 (not_1_out, A);
  and and_1 (and_1_out, A, B);
  xor xor_1 (xor_1_out, A, B);
  Multiplexer #(.select(2), .enable("false")) multiplexer_1 (
    .in0(or_1_out), .in1(not_1_out), .in2(and_1_out), .in3(xor_1_out), .out(F), .sel(Control));
endmodule
