// Logisim project lab4.circ as structural Verilog: 2 circuits, main circuit main
module main (
  input  Qp,
  input  Dp,
  input  Np,
  input  Soda_req,
  input  [3:0] Soda_price,
  input  Clk,
  input  Reset_n,
  output Drop_soda,
  output Amt_err,
  output [6:0] hund_disp_n,
  output [6:0] tens_disp_n,
  output [6:0] ones_disp_n
);

  shell shell_1 (
    .Qp(Qp), .Dp(Dp), .Np(Np), .Soda_req(Soda_req), .Soda_price(Soda_price), .Clk(Clk), .Reset_n(Reset_n),
    .Drop_soda(Drop_soda), .Amt_err(Amt_err), .hund_disp_n(hund_disp_n), .tens_disp_n(tens_disp_n),
    .ones_disp_n(ones_disp_n));
endmodule

module shell (
  input  Qp,
  input  Dp,
  input  Np,
  input  Soda_req,
  input  [3:0] Soda_price,
  input  Clk,
  input  Reset_n,
  output Drop_soda,
  output Amt_err,
  output [6:0] hund_disp_n,
  output [6:0] tens_disp_n,
  output [6:0] ones_disp_n
);


  assign Amt_err = Dp;
  assign Drop_soda = Qp;
endmodule
